# Fritzing sketch Wiring_c12880_test (saved by Fritzing 0.9.4)
breadboards: 1

parts:
  Bauteil1 = Adafruit HUZZAH32 ESP32 Feather [part_number="Adafruit #3405"]
  R1 = Resistor [tolerance=±5% resistance=1.5k package=THT]
  R2 = Resistor [tolerance=±5% resistance=1k package=THT]

nets:
  N1: Bauteil1.A4_IO36, R1.Pin_1, R2.Pin_0
  N2: Bauteil1.GND, R1.Pin_0
