# Fritzing sketch board_v1_fill (saved by Fritzing 0.9.4)
circuit board: 6.4cm x 6.4cm
breadboards: 1

parts:
  huzzah32 = Adafruit HUZZAH32 ESP32 Feather [part_number="Adafruit #3405"]
  R1 = Resistor [tolerance=±5% resistance=1.5k package=THT]
  R2 = Resistor [tolerance=±5% resistance=1k package=THT]
  spect = female pin header, 6 pins [form="♀ (female)"]
  i2c2 = female pin header, 4 pins [form="♀ (female)"]
  R3 = Resistor [tolerance=±5% resistance=8.2k package=THT]
  R4 = Resistor [tolerance=±5% resistance=8.2k package=THT]
  i2c1 = female pin header, 4 pins [form="♀ (female)"]
  com = female pin header, 4 pins [form="♀ (female)"]
  pan = female pin header, 3 pins [form="♀ (female)"]
  tilt = female pin header, 3 pins [form="♀ (female)"]
  sw_5V = Toggle Switch [package=THT]
  J1 = female pin header, 2 pins [form="♀ (female)"]
  VCC_5V = USB Connectors [package=usb-b-pth]
  sw_bat = Toggle Switch [package=THT]
  LiPo_Battery_1100_mAh2 = Lithium Ion Polymer Battery 3.7v 350mAh [part_number=2750]
  J2 = female pin header, 2 pins [form="♀ (female)"]
  neopix = female pin header, 3 pins [form="♀ (female)"]
  R5 = Resistor [tolerance=±5% resistance=680 package=THT]

nets:
  N1: huzzah32.IO21, spect.pin5
  N2: huzzah32.IO17, com.pin3
  N3: huzzah32.IO16, com.pin4
  N4: huzzah32.A4_IO36, R1.Pin_1, R2.Pin_0
  GND: huzzah32.GND, R1.Pin_0, spect.pin2, i2c2.pin2, i2c1.pin2, com.pin2, pan.pin1, tilt.pin1, VCC_5V.GND, LiPo_Battery_1100_mAh2.negative, neopix.pin3
  N5: huzzah32.3.3V, spect.pin1, i2c2.pin1, R3.Pin_1, R4.Pin_1, i2c1.pin1
  N6: huzzah32.VBAT, sw_bat.COM
  N7: huzzah32.IO27_A10, pan.pin3
  N8: huzzah32.IO33_A9, tilt.pin3
  N9: huzzah32.IO15_A8, spect.pin4
  N10: huzzah32.IO32_A7, R5.Pin_0
  N11: huzzah32.IO14_A6, spect.pin3
  N12: huzzah32.SCL, i2c2.pin4, R4.Pin_0, i2c1.pin4
  N13: huzzah32.SDA, i2c2.pin3, R3.Pin_0, i2c1.pin3
  N14: R2.Pin_1, spect.pin6
  N15: com.pin1, pan.pin2, tilt.pin2, sw_5V.COM, neopix.pin2
  N16: sw_5V.L2, J1.pin1
  N17: J1.pin2, VCC_5V.VBUS
  N18: sw_bat.L2, J2.pin1
  N19: LiPo_Battery_1100_mAh2.positive, J2.pin2
  N20: neopix.pin1, R5.Pin_1

notes:
  gnd
  5v
  d
  vid
  rx
  tx
  off
  3v3
  sda
  scl
  3
  g
  sd
  sc
  clk
  sta
  trg
  3V
  (+)
  (-)
  (c) 2020 Euler lab
  Y. Qiu, Z. Zhao, T. Euler
  Spectral Scanner v1.0

custom parts:
  Lithium Ion Polymer Battery 3.7v 350mAh: Lithium ion polymer (also known as 'lipo' or 'lipoly') batteries are thin, light and powerful. The output ranges from 4.2V when completely charged to 3.7V. This battery has a capacity of 350mAh for a total of about 1.3 Wh. The batteries come pre-attached with a genuine 2-pin JST-PH connector as shown and include the necessary protection circuitry.
